# Fritzing sketch weatherstation (saved by Fritzing 1.0.2b)

parts:
  MCU1 = Raspberry Pi Zero
  M1 = RioRand LM2596
  M2 = RioRand LM2596
  M3 = RioRand LM2596
  M4 = DC Motor [voltage_(max)=6V voltage_(min)=3V]
  Bauteil1 = Barometric Pressure Sensor - BMP180 Breakout (GY-68)
  Bauteil2 = Solar Cell
  Bauteil3 = Solar Cell
  Bat1 = battery_holder_single_18650
  Bat2 = battery_holder_single_18650
  Mod1 = YL-83 Rain Sensor - Detection Board
  YL-83_-_Control_Board1 = YL-83 Rain Sensor - Control Board
  Bauteil4 = ADS1115
  M5 = TP4056 Module [part_number=HW-107]

nets:
  VCC: MCU1.pin_1, MCU1.pin_17, YL-83_-_Control_Board1.VCC, Bauteil4.VDD
  N1: MCU1.pin_2, MCU1.pin_4, M3.Pin_3, Bauteil1.VCC
  N2: MCU1.pin_3, Bauteil4.SDA
  N3: MCU1.pin_5, Bauteil4.SCL
  GND: MCU1.pin_6, MCU1.pin_9, MCU1.pin_14, MCU1.pin_20, M3.Pin_4, Bauteil1.GND, YL-83_-_Control_Board1.GND, Bauteil4.GND
  N4: MCU1.pin_12, YL-83_-_Control_Board1.DO
  N5: M1.Pin_3, M2.Pin_3
  N6: M1.Pin_4, M2.Pin_4
  N7: M2.Pin_2, Bauteil3.+
  N8: M3.Pin_1, M5.OUT-#1
  N9: M3.Pin_2, M5.OUT-#4
  N10: M4.pin_2, Bauteil4.A2
  N11: Bauteil2.-, Bauteil3.-
  N12: Bat1.+#0, M5.BAT+
  N13: Bat1.+#1, M5.BAT-
  N14: Bat2.+#0, Bauteil4.A0
  N15: Mod1.POS, YL-83_-_Control_Board1.POS
  N16: Mod1.NEG, YL-83_-_Control_Board1.NEG

custom parts:
  battery_holder_single_18650: single 18650 battery holder
  YL-83 Rain Sensor - Detection Board: The YL-83 is a rain sensor that has more resistance when dry and less resistance when wet. The module runs at 5V.
  YL-83 Rain Sensor - Control Board: The YL-83 is a rain sensor that has more resistance when dry and less resistance when wet. The module runs at 5V.
  ADS1115: ADC ADS1115
  TP4056 Module: TP4056 Lithium Battery Charge Management Module Links: TP4056 website
